// Logisim project SR_latch.circ as structural Verilog: 1 circuit, main circuit main
module main (
  input  S,
  input  R,
  output Q_not,
  output Q
);

  nor nor_1 (Q_not, S, Q);
  nor nor_2 (Q, Q_not, R);
endmodule
